# Fritzing sketch ttcc (saved by Fritzing 0.9.6b)
circuit board: 33.04cm x 22.56cm
breadboards: 1

parts:
  MX50 = Cherry MX Keyswitch Simple
  MX51 = Cherry MX Keyswitch Simple
  MX52 = Cherry MX Keyswitch Simple
  MX53 = Cherry MX Keyswitch Simple
  MX54 = Cherry MX Keyswitch Simple
  MX55 = Cherry MX Keyswitch Simple
  MX56 = Cherry MX Keyswitch Simple
  MX57 = Cherry MX Keyswitch Simple
  MX60 = Cherry MX Keyswitch Simple
  MX61 = Cherry MX Keyswitch Simple
  MX62 = Cherry MX Keyswitch Simple
  MX63 = Cherry MX Keyswitch Simple
  MX65 = Cherry MX Keyswitch Simple
  MX66 = Cherry MX Keyswitch Simple
  MX68 = Cherry MX Keyswitch Simple
  MX69 = Cherry MX Keyswitch Simple
  MX70 = Cherry MX Keyswitch Simple
  MX71 = Cherry MX Keyswitch Simple
  MX72 = Cherry MX Keyswitch Simple
  MX73 = Cherry MX Keyswitch Simple
  MX75 = Cherry MX Keyswitch Simple
  MX77 = Cherry MX Keyswitch Simple
  MX78 = Cherry MX Keyswitch Simple
  MX79 = Cherry MX Keyswitch Simple
  MX80 = Cherry MX Keyswitch Simple
  MX81 = Cherry MX Keyswitch Simple
  MX82 = Cherry MX Keyswitch Simple
  MX83 = Cherry MX Keyswitch Simple
  MX84 = Cherry MX Keyswitch Simple
  MX85 = Cherry MX Keyswitch Simple
  MX86 = Cherry MX Keyswitch Simple
  MX87 = Cherry MX Keyswitch Simple
  MX88 = Cherry MX Keyswitch Simple
  MX89 = Cherry MX Keyswitch Simple
  MX90 = Cherry MX Keyswitch Simple
  MX91 = Cherry MX Keyswitch Simple
  MX92 = Cherry MX Keyswitch Simple
  MX93 = Cherry MX Keyswitch Simple
  MX94 = Cherry MX Keyswitch Simple
  MX95 = Cherry MX Keyswitch Simple
  MX96 = Cherry MX Keyswitch Simple
  MX97 = Cherry MX Keyswitch Simple
  MX98 = Cherry MX Keyswitch Simple
  MX99 = Cherry MX Keyswitch Simple
  MX100 = Cherry MX Keyswitch Simple
  MX101 = Cherry MX Keyswitch Simple
  MX102 = Cherry MX Keyswitch Simple
  MX103 = Cherry MX Keyswitch Simple
  MX104 = Cherry MX Keyswitch Simple
  MX105 = Cherry MX Keyswitch Simple
  MX106 = Cherry MX Keyswitch Simple
  MX107 = Cherry MX Keyswitch Simple
  MX108 = Cherry MX Keyswitch Simple
  MX109 = Cherry MX Keyswitch Simple
  MX110 = Cherry MX Keyswitch Simple
  MX111 = Cherry MX Keyswitch Simple
  MX112 = Cherry MX Keyswitch Simple
  MX113 = Cherry MX Keyswitch Simple
  MX114 = Cherry MX Keyswitch Simple
  MX115 = Cherry MX Keyswitch Simple
  MX116 = Cherry MX Keyswitch Simple
  MX117 = Cherry MX Keyswitch Simple
  MX118 = Cherry MX Keyswitch Simple
  MX119 = Cherry MX Keyswitch Simple
  MX120 = Cherry MX Keyswitch Simple
  MX121 = Cherry MX Keyswitch Simple
  MX122 = Cherry MX Keyswitch Simple
  MX123 = Cherry MX Keyswitch Simple
  MX124 = Cherry MX Keyswitch Simple
  MX125 = Cherry MX Keyswitch Simple
  MX126 = Cherry MX Keyswitch Simple
  MX127 = Cherry MX Keyswitch Simple
  MX131 = Cherry MX Keyswitch Simple
  MX133 = Cherry MX Keyswitch Simple
  MX134 = Cherry MX Keyswitch Simple
  MX135 = Cherry MX Keyswitch Simple
  MX136 = Cherry MX Keyswitch Simple
  MX138 = Cherry MX Keyswitch Simple
  MX139 = Cherry MX Keyswitch Simple
  MX140 = Cherry MX Keyswitch Simple
  MX141 = Cherry MX Keyswitch Simple
  MX142 = Cherry MX Keyswitch Simple
  MX143 = Cherry MX Keyswitch Simple
  MX146 = Cherry MX Keyswitch Simple
  MX147 = Cherry MX Keyswitch Simple
  MX149 = Cherry MX Keyswitch Simple
  MX150 = Cherry MX Keyswitch Simple
  MX151 = Cherry MX Keyswitch Simple
  MX152 = Cherry MX Keyswitch Simple
  MX153 = Cherry MX Keyswitch Simple
  MX154 = Cherry MX Keyswitch Simple
  MX155 = Cherry MX Keyswitch Simple
  MX156 = Cherry MX Keyswitch Simple
  MX157 = Cherry MX Keyswitch Simple
  MX158 = Cherry MX Keyswitch Simple
  MX159 = Cherry MX Keyswitch Simple
  MX162 = Cherry MX Keyswitch Simple
  MX165 = Cherry MX Keyswitch Simple
  MX166 = Cherry MX Keyswitch Simple
  MX168 = Cherry MX Keyswitch Simple
  MX169 = Cherry MX Keyswitch Simple
  MX171 = Cherry MX Keyswitch Simple
  MX172 = Cherry MX Keyswitch Simple
  MX173 = Cherry MX Keyswitch Simple
  MX175 = Cherry MX Keyswitch Simple
  MX178 = Cherry MX Keyswitch Simple
  MX181 = Cherry MX Keyswitch Simple
  MX182 = Cherry MX Keyswitch Simple
  MX184 = Cherry MX Keyswitch Simple
  MX185 = Cherry MX Keyswitch Simple
  MX187 = Cherry MX Keyswitch Simple
  MX188 = Cherry MX Keyswitch Simple
  MX189 = Cherry MX Keyswitch Simple
  MX191 = Cherry MX Keyswitch Simple
  MX193 = Cherry MX Keyswitch Simple
  MX194 = Cherry MX Keyswitch Simple
  MX195 = Cherry MX Keyswitch Simple
  MX196 = Cherry MX Keyswitch Simple
  MX197 = Cherry MX Keyswitch Simple
  MX198 = Cherry MX Keyswitch Simple
  MX199 = Cherry MX Keyswitch Simple
  MX200 = Cherry MX Keyswitch Simple
  MX201 = Cherry MX Keyswitch Simple
  MX202 = Cherry MX Keyswitch Simple
  MX203 = Cherry MX Keyswitch Simple
  MX204 = Cherry MX Keyswitch Simple
  MX205 = Cherry MX Keyswitch Simple
  MX206 = Cherry MX Keyswitch Simple
  MX207 = Cherry MX Keyswitch Simple
  MX209 = Cherry MX Keyswitch Simple
  MX210 = Cherry MX Keyswitch Simple
  MX211 = Cherry MX Keyswitch Simple
  MX212 = Cherry MX Keyswitch Simple
  MX213 = Cherry MX Keyswitch Simple
  MX214 = Cherry MX Keyswitch Simple
  MX215 = Cherry MX Keyswitch Simple
  MX216 = Cherry MX Keyswitch Simple
  MX217 = Cherry MX Keyswitch Simple
  MX218 = Cherry MX Keyswitch Simple
  MX219 = Cherry MX Keyswitch Simple
  MX220 = Cherry MX Keyswitch Simple
  MX221 = Cherry MX Keyswitch Simple
  MX222 = Cherry MX Keyswitch Simple
  MX223 = Cherry MX Keyswitch Simple
  MX224 = Cherry MX Keyswitch Simple
  MX225 = Cherry MX Keyswitch Simple
  MX226 = Cherry MX Keyswitch Simple
  MX227 = Cherry MX Keyswitch Simple
  MX228 = Cherry MX Keyswitch Simple
  MX229 = Cherry MX Keyswitch Simple
  MX230 = Cherry MX Keyswitch Simple
  MX231 = Cherry MX Keyswitch Simple
  MX232 = Cherry MX Keyswitch Simple
  MX233 = Cherry MX Keyswitch Simple
  MX234 = Cherry MX Keyswitch Simple
  MX235 = Cherry MX Keyswitch Simple
  MX236 = Cherry MX Keyswitch Simple
  MX237 = Cherry MX Keyswitch Simple
  MX238 = Cherry MX Keyswitch Simple
  D1 = Rectifier Diode [part_number=1N4001 package="300 mil [THT]"]
  D2 = Rectifier Diode [part_number=1N4001 package="300 mil [THT]"]
  D3 = Rectifier Diode [part_number=1N4001 package="300 mil [THT]"]
  D4 = Rectifier Diode [part_number=1N4001 package="300 mil [THT]"]
  D5 = Rectifier Diode [part_number=1N4001 package="300 mil [THT]"]
  D6 = Rectifier Diode [part_number=1N4001 package="300 mil [THT]"]
  D7 = Rectifier Diode [part_number=1N4001 package="300 mil [THT]"]
  D8 = Rectifier Diode [part_number=1N4001 package="300 mil [THT]"]
  D9 = Rectifier Diode [part_number=1N4001 package="300 mil [THT]"]
  D10 = Rectifier Diode [part_number=1N4001 package="300 mil [THT]"]
  D11 = Rectifier Diode [part_number=1N4001 package="300 mil [THT]"]
  D12 = Rectifier Diode [part_number=1N4001 package="300 mil [THT]"]
  D13 = Rectifier Diode [part_number=1N4001 package="300 mil [THT]"]
  D14 = Rectifier Diode [part_number=1N4001 package="300 mil [THT]"]
  D15 = Rectifier Diode [part_number=1N4001 package="300 mil [THT]"]
  D16 = Rectifier Diode [part_number=1N4001 package="300 mil [THT]"]
  D17 = Rectifier Diode [part_number=1N4001 package="300 mil [THT]"]
  D18 = Rectifier Diode [part_number=1N4001 package="300 mil [THT]"]
  D19 = Rectifier Diode [part_number=1N4001 package="300 mil [THT]"]
  D20 = Rectifier Diode [part_number=1N4001 package="300 mil [THT]"]
  D21 = Rectifier Diode [part_number=1N4001 package="300 mil [THT]"]
  D22 = Rectifier Diode [part_number=1N4001 package="300 mil [THT]"]
  D23 = Rectifier Diode [part_number=1N4001 package="300 mil [THT]"]
  D24 = Rectifier Diode [part_number=1N4001 package="300 mil [THT]"]
  D25 = Rectifier Diode [part_number=1N4001 package="300 mil [THT]"]
  D26 = Rectifier Diode [part_number=1N4001 package="300 mil [THT]"]
  D27 = Rectifier Diode [part_number=1N4001 package="300 mil [THT]"]
  D28 = Rectifier Diode [part_number=1N4001 package="300 mil [THT]"]
  D29 = Rectifier Diode [part_number=1N4001 package="300 mil [THT]"]
  D30 = Rectifier Diode [part_number=1N4001 package="300 mil [THT]"]
  D31 = Rectifier Diode [part_number=1N4001 package="300 mil [THT]"]
  D32 = Rectifier Diode [part_number=1N4001 package="300 mil [THT]"]
  D33 = Rectifier Diode [part_number=1N4001 package="300 mil [THT]"]
  D34 = Rectifier Diode [part_number=1N4001 package="300 mil [THT]"]
  D35 = Rectifier Diode [part_number=1N4001 package="300 mil [THT]"]
  D36 = Rectifier Diode [part_number=1N4001 package="300 mil [THT]"]
  D37 = Rectifier Diode [part_number=1N4001 package="300 mil [THT]"]
  D38 = Rectifier Diode [part_number=1N4001 package="300 mil [THT]"]
  D39 = Rectifier Diode [part_number=1N4001 package="300 mil [THT]"]
  D40 = Rectifier Diode [part_number=1N4001 package="300 mil [THT]"]
  D41 = Rectifier Diode [part_number=1N4001 package="300 mil [THT]"]
  D42 = Rectifier Diode [part_number=1N4001 package="300 mil [THT]"]
  D43 = Rectifier Diode [part_number=1N4001 package="300 mil [THT]"]
  D44 = Rectifier Diode [part_number=1N4001 package="300 mil [THT]"]
  D45 = Rectifier Diode [part_number=1N4001 package="300 mil [THT]"]
  D46 = Rectifier Diode [part_number=1N4001 package="300 mil [THT]"]
  D47 = Rectifier Diode [part_number=1N4001 package="300 mil [THT]"]
  D48 = Rectifier Diode [part_number=1N4001 package="300 mil [THT]"]
  D49 = Rectifier Diode [part_number=1N4001 package="300 mil [THT]"]
  D50 = Rectifier Diode [part_number=1N4001 package="300 mil [THT]"]
  D51 = Rectifier Diode [part_number=1N4001 package="300 mil [THT]"]
  D52 = Rectifier Diode [part_number=1N4001 package="300 mil [THT]"]
  D53 = Rectifier Diode [part_number=1N4001 package="300 mil [THT]"]
  D54 = Rectifier Diode [part_number=1N4001 package="300 mil [THT]"]
  D55 = Rectifier Diode [part_number=1N4001 package="300 mil [THT]"]
  D56 = Rectifier Diode [part_number=1N4001 package="300 mil [THT]"]
  D57 = Rectifier Diode [part_number=1N4001 package="300 mil [THT]"]
  D58 = Rectifier Diode [part_number=1N4001 package="300 mil [THT]"]
  D59 = Rectifier Diode [part_number=1N4001 package="300 mil [THT]"]
  D60 = Rectifier Diode [part_number=1N4001 package="300 mil [THT]"]
  D61 = Rectifier Diode [part_number=1N4001 package="300 mil [THT]"]
  D62 = Rectifier Diode [part_number=1N4001 package="300 mil [THT]"]
  D63 = Rectifier Diode [part_number=1N4001 package="300 mil [THT]"]
  D64 = Rectifier Diode [part_number=1N4001 package="300 mil [THT]"]
  D65 = Rectifier Diode [part_number=1N4001 package="300 mil [THT]"]
  D66 = Rectifier Diode [part_number=1N4001 package="300 mil [THT]"]
  D67 = Rectifier Diode [part_number=1N4001 package="300 mil [THT]"]
  D68 = Rectifier Diode [part_number=1N4001 package="300 mil [THT]"]
  D69 = Rectifier Diode [part_number=1N4001 package="300 mil [THT]"]
  D70 = Rectifier Diode [part_number=1N4001 package="300 mil [THT]"]
  D71 = Rectifier Diode [part_number=1N4001 package="300 mil [THT]"]
  D72 = Rectifier Diode [part_number=1N4001 package="300 mil [THT]"]
  D73 = Rectifier Diode [part_number=1N4001 package="300 mil [THT]"]
  D74 = Rectifier Diode [part_number=1N4001 package="300 mil [THT]"]
  D76 = Rectifier Diode [part_number=1N4001 package="300 mil [THT]"]
  D77 = Rectifier Diode [part_number=1N4001 package="300 mil [THT]"]
  D78 = Rectifier Diode [part_number=1N4001 package="300 mil [THT]"]
  D79 = Rectifier Diode [part_number=1N4001 package="300 mil [THT]"]
  D80 = Rectifier Diode [part_number=1N4001 package="300 mil [THT]"]
  D81 = Rectifier Diode [part_number=1N4001 package="300 mil [THT]"]
  D82 = Rectifier Diode [part_number=1N4001 package="300 mil [THT]"]
  D83 = Rectifier Diode [part_number=1N4001 package="300 mil [THT]"]
  D84 = Rectifier Diode [part_number=1N4001 package="300 mil [THT]"]
  D85 = Rectifier Diode [part_number=1N4001 package="300 mil [THT]"]
  D86 = Rectifier Diode [part_number=1N4001 package="300 mil [THT]"]
  D87 = Rectifier Diode [part_number=1N4001 package="300 mil [THT]"]
  D88 = Rectifier Diode [part_number=1N4001 package="300 mil [THT]"]
  D89 = Rectifier Diode [part_number=1N4001 package="300 mil [THT]"]
  D90 = Rectifier Diode [part_number=1N4001 package="300 mil [THT]"]
  D91 = Rectifier Diode [part_number=1N4001 package="300 mil [THT]"]
  D92 = Rectifier Diode [part_number=1N4001 package="300 mil [THT]"]
  D93 = Rectifier Diode [part_number=1N4001 package="300 mil [THT]"]
  D94 = Rectifier Diode [part_number=1N4001 package="300 mil [THT]"]
  D95 = Rectifier Diode [part_number=1N4001 package="300 mil [THT]"]
  D96 = Rectifier Diode [part_number=1N4001 package="300 mil [THT]"]
  D97 = Rectifier Diode [part_number=1N4001 package="300 mil [THT]"]
  D98 = Rectifier Diode [part_number=1N4001 package="300 mil [THT]"]
  D99 = Rectifier Diode [part_number=1N4001 package="300 mil [THT]"]
  D100 = Rectifier Diode [part_number=1N4001 package="300 mil [THT]"]
  D101 = Rectifier Diode [part_number=1N4001 package="300 mil [THT]"]
  D102 = Rectifier Diode [part_number=1N4001 package="300 mil [THT]"]
  D103 = Rectifier Diode [part_number=1N4001 package="300 mil [THT]"]
  D104 = Rectifier Diode [part_number=1N4001 package="300 mil [THT]"]
  D105 = Rectifier Diode [part_number=1N4001 package="300 mil [THT]"]
  D106 = Rectifier Diode [part_number=1N4001 package="300 mil [THT]"]
  D107 = Rectifier Diode [part_number=1N4001 package="300 mil [THT]"]
  D108 = Rectifier Diode [part_number=1N4001 package="300 mil [THT]"]
  D109 = Rectifier Diode [part_number=1N4001 package="300 mil [THT]"]
  D110 = Rectifier Diode [part_number=1N4001 package="300 mil [THT]"]
  D111 = Rectifier Diode [part_number=1N4001 package="300 mil [THT]"]
  D112 = Rectifier Diode [part_number=1N4001 package="300 mil [THT]"]
  D113 = Rectifier Diode [part_number=1N4001 package="300 mil [THT]"]
  D114 = Rectifier Diode [part_number=1N4001 package="300 mil [THT]"]
  D115 = Rectifier Diode [part_number=1N4001 package="300 mil [THT]"]
  J16 = female pin header, 14 pins [form="♀ (female)"]
  J17 = female pin header, 14 pins [form="♀ (female)"]

nets:
  N1: MX50.pin_1, D3.cathode
  N2: MX50.pin_2, MX51.pin_2, MX52.pin_2, MX53.pin_2, MX54.pin_2, MX55.pin_2, MX56.pin_2, MX57.pin_2, MX60.pin_2, MX61.pin_2, MX62.pin_2, MX63.pin_2, MX224.pin_2, MX226.pin_2, J17.pin10
  N3: MX51.pin_1, D4.cathode
  N4: MX52.pin_1, D5.cathode
  N5: MX53.pin_1, D6.cathode
  N6: MX54.pin_1, D7.cathode
  N7: MX55.pin_1, D8.cathode
  N8: MX56.pin_1, D16.cathode
  N9: MX57.pin_1, D11.cathode
  N10: MX60.pin_1, D9.cathode
  N11: MX61.pin_1, D14.cathode
  N12: MX62.pin_1, D15.cathode
  N13: MX63.pin_1, D12.cathode
  N14: MX65.pin_1, D27.cathode
  N15: MX65.pin_2, MX66.pin_2, MX68.pin_2, MX69.pin_2, MX70.pin_2, MX71.pin_2, MX72.pin_2, MX73.pin_2, MX75.pin_2, MX77.pin_2, MX78.pin_2, MX79.pin_2, MX225.pin_2, MX227.pin_2, J17.pin11
  N16: MX66.pin_1, D26.cathode
  N17: MX68.pin_1, D19.cathode
  N18: MX69.pin_1, D24.cathode
  N19: MX70.pin_1, D21.cathode
  N20: MX71.pin_1, D22.cathode
  N21: MX72.pin_1, D28.cathode
  N22: MX73.pin_1, D17.cathode
  N23: MX75.pin_1, D20.cathode
  N24: MX77.pin_1, D23.cathode
  N25: MX78.pin_1, D18.cathode
  N26: MX79.pin_1, D25.cathode
  N27: MX80.pin_1, D44.cathode
  N28: MX80.pin_2, MX81.pin_2, MX82.pin_2, MX83.pin_2, MX84.pin_2, MX85.pin_2, MX86.pin_2, MX87.pin_2, MX88.pin_2, MX89.pin_2, MX90.pin_2, MX91.pin_2, MX92.pin_2, MX93.pin_2, MX94.pin_2, MX95.pin_2, J17.pin12
  N29: MX81.pin_1, D34.cathode
  N30: MX82.pin_1, D41.cathode
  N31: MX83.pin_1, D38.cathode
  N32: MX84.pin_1, D37.cathode
  N33: MX85.pin_1, D36.cathode
  N34: MX86.pin_1, D35.cathode
  N35: MX87.pin_1, D33.cathode
  N36: MX88.pin_1, D39.cathode
  N37: MX89.pin_1, D43.cathode
  N38: MX90.pin_1, D31.cathode
  N39: MX91.pin_1, D32.cathode
  N40: MX92.pin_1, D40.cathode
  N41: MX93.pin_1, D30.cathode
  N42: MX94.pin_1, D42.cathode
  N43: MX95.pin_1, D29.cathode
  N44: MX96.pin_1, D60.cathode
  N45: MX96.pin_2, MX97.pin_2, MX98.pin_2, MX99.pin_2, MX100.pin_2, MX101.pin_2, MX102.pin_2, MX103.pin_2, MX104.pin_2, MX105.pin_2, MX106.pin_2, MX107.pin_2, MX108.pin_2, MX109.pin_2, MX110.pin_2, MX111.pin_2, J17.pin13
  N46: MX97.pin_1, D50.cathode
  N47: MX98.pin_1, D57.cathode
  N48: MX99.pin_1, D54.cathode
  N49: MX100.pin_1, D53.cathode
  N50: MX101.pin_1, D52.cathode
  N51: MX102.pin_1, D51.cathode
  N52: MX103.pin_1, D49.cathode
  N53: MX104.pin_1, D55.cathode
  N54: MX105.pin_1, D59.cathode
  N55: MX106.pin_1, D47.cathode
  N56: MX107.pin_1, D48.cathode
  N57: MX108.pin_1, D56.cathode
  N58: MX109.pin_1, D46.cathode
  N59: MX110.pin_1, D58.cathode
  N60: MX111.pin_1, D45.cathode
  N61: MX112.pin_1, D76.cathode
  N62: MX112.pin_2, MX113.pin_2, MX114.pin_2, MX115.pin_2, MX116.pin_2, MX117.pin_2, MX118.pin_2, MX119.pin_2, MX120.pin_2, MX121.pin_2, MX122.pin_2, MX123.pin_2, MX124.pin_2, MX125.pin_2, MX126.pin_2, MX127.pin_2, MX146.pin_2, MX153.pin_2, J17.pin14
  N63: MX113.pin_1, D66.cathode
  N64: MX114.pin_1, MX121.pin_1, MX146.pin_1, MX153.pin_1, D73.cathode
  N65: MX115.pin_1, D70.cathode
  N66: MX116.pin_1, D69.cathode
  N67: MX117.pin_1, D68.cathode
  N68: MX118.pin_1, D67.cathode
  N69: MX119.pin_1, D65.cathode
  N70: MX120.pin_1, D71.cathode
  N71: MX122.pin_1, D63.cathode
  N72: MX123.pin_1, D64.cathode
  N73: MX124.pin_1, D72.cathode
  N74: MX125.pin_1, D62.cathode
  N75: MX126.pin_1, D74.cathode
  N76: MX127.pin_1, D61.cathode
  N77: MX131.pin_1, D86.cathode
  N78: MX131.pin_2, MX133.pin_2, MX134.pin_2, MX135.pin_2, MX136.pin_2, MX138.pin_2, MX139.pin_2, MX140.pin_2, MX141.pin_2, MX142.pin_2, MX143.pin_2, MX147.pin_2, MX149.pin_2, MX150.pin_2, MX151.pin_2, MX152.pin_2, MX154.pin_2, MX155.pin_2, MX156.pin_2, MX157.pin_2, MX158.pin_2, MX159.pin_2, MX228.pin_2, MX231.pin_2, MX232.pin_2, J16.pin14
  N79: MX133.pin_1, MX143.pin_1, MX149.pin_1, MX159.pin_1, D77.cathode
  N80: MX134.pin_1, MX141.pin_1, MX150.pin_1, MX157.pin_1, D78.cathode
  N81: MX135.pin_1, MX142.pin_1, MX151.pin_1, MX158.pin_1, D84.cathode
  N82: MX136.pin_1, MX139.pin_1, MX152.pin_1, MX155.pin_1, D87.cathode
  N83: MX138.pin_1, D85.cathode
  N84: MX140.pin_1, D80.cathode
  N85: MX147.pin_1, D89.cathode
  N86: MX154.pin_1, D88.cathode
  N87: MX156.pin_1, D81.cathode
  N88: MX162.pin_1, MX169.pin_1, MX178.pin_1, MX185.pin_1, D92.cathode
  N89: MX162.pin_2, MX165.pin_2, MX166.pin_2, MX168.pin_2, MX169.pin_2, MX171.pin_2, MX172.pin_2, MX173.pin_2, MX175.pin_2, MX178.pin_2, MX181.pin_2, MX182.pin_2, MX184.pin_2, MX185.pin_2, MX187.pin_2, MX188.pin_2, MX189.pin_2, MX191.pin_2, MX229.pin_2, MX233.pin_2, MX234.pin_2, MX235.pin_2, MX236.pin_2, MX237.pin_2, MX238.pin_2, J16.pin13
  N90: MX165.pin_1, MX175.pin_1, MX181.pin_1, MX191.pin_1, D93.cathode
  N91: MX166.pin_1, MX173.pin_1, MX182.pin_1, MX189.pin_1, D91.cathode
  N92: MX168.pin_1, MX171.pin_1, MX184.pin_1, MX187.pin_1, D108.cathode
  N93: MX172.pin_1, D94.cathode
  N94: MX188.pin_1, D90.cathode
  N95: MX193.pin_1, D110.cathode
  N96: MX193.pin_2, MX194.pin_2, MX195.pin_2, MX196.pin_2, MX197.pin_2, MX198.pin_2, MX199.pin_2, MX200.pin_2, MX201.pin_2, MX202.pin_2, MX203.pin_2, MX204.pin_2, MX205.pin_2, MX206.pin_2, MX207.pin_2, MX209.pin_2, MX210.pin_2, MX211.pin_2, MX212.pin_2, MX213.pin_2, MX214.pin_2, MX215.pin_2, MX216.pin_2, MX217.pin_2, MX218.pin_2, MX219.pin_2, MX220.pin_2, MX221.pin_2, MX222.pin_2, MX223.pin_2, MX230.pin_2, J16.pin12
  N97: MX194.pin_1, MX201.pin_1, MX210.pin_1, MX217.pin_1, D101.cathode
  N98: MX195.pin_1, MX202.pin_1, MX211.pin_1, MX218.pin_1, D115.cathode
  N99: MX196.pin_1, D113.cathode
  N100: MX197.pin_1, MX207.pin_1, MX213.pin_1, MX223.pin_1, D97.cathode
  N101: MX198.pin_1, MX205.pin_1, MX214.pin_1, MX221.pin_1, D96.cathode
  N102: MX199.pin_1, MX206.pin_1, MX215.pin_1, MX222.pin_1, D114.cathode
  N103: MX200.pin_1, MX203.pin_1, MX216.pin_1, MX219.pin_1, D109.cathode
  N104: MX204.pin_1, D100.cathode
  N105: MX209.pin_1, D111.cathode
  N106: MX212.pin_1, D112.cathode
  N107: MX220.pin_1, D98.cathode
  N108: MX224.pin_1, D1.cathode
  N109: MX225.pin_1, D2.cathode
  N110: MX226.pin_1, D13.cathode
  N111: MX227.pin_1, D10.cathode
  N112: MX228.pin_1, D79.cathode
  N113: MX229.pin_1, D95.cathode
  N114: MX230.pin_1, D99.cathode
  N115: MX231.pin_1, D82.cathode
  N116: MX232.pin_1, D83.cathode
  N117: MX233.pin_1, D105.cathode
  N118: MX234.pin_1, D102.cathode
  N119: MX235.pin_1, D103.cathode
  N120: MX236.pin_1, D104.cathode
  N121: MX237.pin_1, D107.cathode
  N122: MX238.pin_1, D106.cathode
  N123: D1.anode, D40.anode, D56.anode, D72.anode, D80.anode, D94.anode, D100.anode, J17.pin2
  N124: D2.anode, D44.anode, D60.anode, D76.anode, D81.anode, D90.anode, D98.anode, J17.pin3
  N125: D3.anode, D23.anode, D30.anode, D46.anode, D62.anode, D79.anode, D95.anode, D99.anode, J17.pin4
  N126: D4.anode, D21.anode, D35.anode, D51.anode, D67.anode, D78.anode, D91.anode, D96.anode, J17.pin5
  N127: D5.anode, D24.anode, D36.anode, D52.anode, D68.anode, J17.pin7
  N128: D6.anode, D25.anode, D29.anode, D45.anode, D61.anode, D77.anode, D93.anode, D97.anode, J17.pin6
  N129: D7.anode, D26.anode, D41.anode, D57.anode, D73.anode, D92.anode, D101.anode, J17.pin8
  N130: D8.anode, D17.anode, D43.anode, D59.anode, J17.pin9
  N131: D9.anode, D18.anode, D42.anode, D58.anode, D74.anode, D83.anode, D102.anode, D113.anode, J16.pin8
  N132: D10.anode, D31.anode, D47.anode, D63.anode, D88.anode, D106.anode, D115.anode, J16.pin4
  N133: D11.anode, D28.anode, D39.anode, D55.anode, D71.anode, D84.anode, J16.pin10
  N134: D12.anode, D27.anode, D34.anode, D50.anode, D66.anode, D89.anode, D104.anode, D110.anode, J16.pin6
  N135: D13.anode, D38.anode, D54.anode, D70.anode, D85.anode, D107.anode, D111.anode, J16.pin5
  N136: D14.anode, D20.anode, D32.anode, D48.anode, D64.anode, D87.anode, D108.anode, D109.anode, J16.pin11
  N137: D15.anode, D19.anode, D37.anode, D53.anode, D69.anode, D86.anode, D103.anode, D112.anode, J16.pin7
  N138: D16.anode, D22.anode, D33.anode, D49.anode, D65.anode, D82.anode, D105.anode, D114.anode, J16.pin9

notes:
  1
  0
  GD
  10
  9
  8
  7
  6
  5
  4
  3
  2
  15
  17
  19
  21
  16
  18
  20
  22
  23
  3V
  VI
  12
  11
  13
  14
  Two Thirds California Case Keyboard
  https://github.com/RebeccaRGB/ttcc
  330.4 x 225.6

custom parts:
  Cherry MX Keyswitch Simple: Cherry MX Keyswitch button for keyboards
